// Logisim project 522H0068_PhamVanPhuc_Lab3_Cau 1.circ as structural Verilog: 1 circuit, main circuit main
module main (
  input  in_1,
  input  in_2,
  input  in_3,
  input  in_4,
  input  [3:0] in_5
);

  LED led_1 (.in(in_5[2]));
  LED led_2 (.in(in_5[3]));
  Hex_Digit_Display hex_digit_display_1 (.value({in_1, in_2, in_3, in_4}));  // open: dp
  LED led_3 (.in(in_5[1]));
  LED led_4 (.in(in_5[0]));
  Hex_Digit_Display hex_digit_display_2 (.value(in_5));  // open: dp
endmodule
