// Logisim project 522H0068_PhamVanPhuc_Lab3_Cau2.circ as structural Verilog
module Machcon (
  input  a,
  input  b,
  output s,
  output c
);

  xor xor_1 (s, a, b);
  and and_1 (c, a, b);
endmodule

module Machchinh (
  input  a,
  input  b
);

  wire machcon_1_c, machcon_1_s;

  Machcon machcon_1 (.a(a), .b(b), .s(machcon_1_s), .c(machcon_1_c));
  LED s (.in(machcon_1_s));
  LED c (.in(machcon_1_c));
endmodule
