// Logisim project 522H0068_PhamVanPhuc_Lab3_Cau3.circ as structural Verilog
module cau3 (
  input  a,
  input  b,
  output x,
  output y
);

  wire and_1_out, and_2_out, not_1_out, not_2_out, not_3_out;

  not not_1 (not_1_out, b);
  not not_2 (not_2_out, a);
  not not_3 (not_3_out, b);
  or or_1 (x, not_1_out, a);
  and and_1 (and_1_out, not_2_out, b);
  and and_2 (and_2_out, a, not_3_out);
  or or_2 (y, and_1_out, and_2_out);
endmodule
