// Logisim project 522H0068_PhamVanPhuc_Lab3_Cau4.circ as structural Verilog: 1 circuit, main circuit main
module main (
  input  a
);

  Clock clock_1 (.out(a));
  LED led_1 (.in(a));
  LED led_2 (.in(a));
  LED led_3 (.in(a));

  // Notes on the sheet:
  //   clock
  //   LED
endmodule
