// Logisim project 522H0068_PhamVanPhuc_Lab3_Cau5.circ as structural Verilog: 1 circuit, main circuit main
module main (
);

  wire clock_1_out;
  wire [2:0] counter_1_q, rom_1_data;

  Clock clock_1 (.out(clock_1_out));
  Counter #(.width(3), .max('h7)) counter_1 (
    .count(clock_1_out), .Q(counter_1_q), .clk(clock_1_out));  // open: load, D, carry, clr
  ROM #(.addrWidth(3), .dataWidth(3)) rom_1 (.addr(counter_1_q), .data(rom_1_data));  // open: sel
  LED led_1 (.in(rom_1_data[0]));
  LED led_2 (.in(rom_1_data[1]));
  LED led_3 (.in(rom_1_data[2]));

  // Notes on the sheet:
  //   clock
  //   Traffic Led
  //   contents of rom_1 (hex, n*v repeats v):
  //   1 1 4 4 2 2 1 1
  //   Đèn đỏ
  //   Đèn vàng
  //   Đèn xanh
endmodule
